# Fritzing sketch LedPong (saved by Fritzing 0.9.3b)
breadboards: 1

parts:
  LED1 = LED - 5mm [color="Red (633nm)" package="5 mm [THT]"]
  LED2 = LED - 5mm [color="Green (570nm)" package="5 mm [THT]"]
  LED3 = LED - 5mm [color="Green (570nm)" package="5 mm [THT]"]
  LED4 = LED - 5mm [color="Green (570nm)" package="5 mm [THT]"]
  R1 = Rotary Potentiometer (Small) [maximum_resistance=100kΩ package=THT]
  S1 = Pushbutton [package="[THT]"]
  S2 = Pushbutton [package="[THT]"]
  S3 = Pushbutton [package="[THT]"]
  R2 = Resistor [tolerance=±5% resistance=220 package=THT]
  R3 = Resistor [tolerance=±5% resistance=220 package=THT]
  R4 = Resistor [tolerance=±5% resistance=220 package=THT]
  R5 = Resistor [tolerance=±5% resistance=220 package=THT]
  R6 = Resistor [tolerance=±5% resistance=10k package=THT]
  R7 = Resistor [tolerance=±5% resistance=10k package=THT]
  R8 = Resistor [tolerance=±5% resistance=10k package=THT]
  Componente1 = Arduino Uno (Rev3)

nets:
  N1: LED1.cathode, R5.Pin_1
  N2: LED1.anode, LED2.anode, LED3.anode, LED4.anode, R1.leg1, R6.Pin_0, R7.Pin_0, R8.Pin_0, Componente1.GND
  N3: LED2.cathode, R2.Pin_1
  N4: LED3.cathode, R3.Pin_1
  N5: LED4.cathode, R4.Pin_1
  N6: R1.wiper, Componente1.A0
  N7: R1.leg2, S1.Pin_1, S1.Pin_2, S2.Pin_1, S2.Pin_2, S3.Pin_1, S3.Pin_2, Componente1.5V
  N8: S1.Pin_3, S1.Pin_4, R7.Pin_1, Componente1.D5_PWM
  N9: S2.Pin_3, S2.Pin_4, R6.Pin_1, Componente1.D2
  N10: S3.Pin_3, S3.Pin_4, R8.Pin_1, Componente1.D3_PWM
  N11: R2.Pin_0, Componente1.D7
  N12: R3.Pin_0, Componente1.D12/MISO
  N13: R4.Pin_0, Componente1.D13/SCK
  N14: R5.Pin_0, Componente1.D9_PWM
