# Fritzing sketch SmartGH (saved by Fritzing 0.9.3b)
breadboards: 1

parts:
  Componente1 = Arduino Uno (Rev3)
  U1 = NodeMCU V1.0
  RHT1 = Humidity and Temperature Sensor RHT03
  HC-SR04_Sensor_1 = HC-SR04 Ultrasonic Distance Sensor
  Componente2 = Bluetooth HC-05 Macho
  J1 = Basic Servo
  LED1 = LED - 5mm [color="Red (633nm)" package="5 mm [THT]"]
  LED2 = LED - 5mm [color="Green (570nm)" package="5 mm [THT]"]
  LED3 = LED - 5mm [color="Green (570nm)" package="5 mm [THT]"]
  R1 = Resistor [tolerance=±5% resistance=220 package=THT]
  R2 = Resistor [tolerance=±5% resistance=220 package=THT]
  R3 = Resistor [tolerance=±5% resistance=220 package=THT]

nets:
  N1: Componente1.D8, HC-SR04_Sensor_1.ECHO
  N2: Componente1.D11_PWM/MOSI, R1.Pin_1
  N3: Componente1.D12/MISO, R2.Pin_1
  N4: Componente1.D13/SCK, R3.Pin_1
  N5: Componente1.D2, Componente2.TXD
  N6: Componente1.D4, Componente2.RXD
  N7: Componente1.D7, HC-SR04_Sensor_1.TRIG
  VCC: Componente1.5V, HC-SR04_Sensor_1.VCC, Componente2.VCC, J1.vcc
  GND: Componente1.GND, HC-SR04_Sensor_1.GND, Componente2.GND, J1.gnd, LED1.anode, LED3.anode
  N8: U1.D4, RHT1.Data-signal
  3V3: U1.3V3, RHT1.Vcc
  N9: U1.GND, RHT1.GND_1
  N10: LED1.cathode, R3.Pin_0
  N11: LED2.cathode, R2.Pin_0
  N12: LED3.cathode, R1.Pin_0

custom parts:
  NodeMCU V1.0: ESP8266 based NodeMCU
